# Fritzing sketch pump_fritzing_layout_v6 (saved by Fritzing 0.9.4)
perfboards: 1

parts:
  Part1 = Arduino Uno (Rev3)
  M1 = DC Motor
  R1 = Resistor [tolerance=±5% resistance=10k package=THT]
  D2 = Schottky Diode [part_number=1N5817 package="300 mil [THT]"]
  Q2 = MOSFET-NCHANNEL [package=to220v]
  12V = Battery block 9V
  Terminal_block = Camdenboss CTB0158-7 [part_number=CTB0158-7 package=THT]
  R2 = Resistor [tolerance=±5% resistance=100 package=THT]

nets:
  N1: Part1.D12/MISO, Terminal_block.terminal_6
  N2: Part1.GND, Terminal_block.terminal_1
  N3: M1.pin_1, Terminal_block.terminal_4
  N4: M1.pin_2, Terminal_block.terminal_5
  N5: R1.Pin_0, Q2.G, R2.Pin_0
  N6: R1.Pin_1, Q2.S, Terminal_block.pin1, Terminal_block.pin2
  N7: D2.cathode, Q2.D, Terminal_block.pin5
  N8: D2.anode, Terminal_block.pin3, Terminal_block.pin4
  N9: 12V.-, Terminal_block.terminal_2
  N10: 12V.+, Terminal_block.terminal_3
  N11: Terminal_block.pin6, R2.Pin_1

notes:
  ---- Current parts used -----
  [1] 100 ohm reistor As shown Generic
  [2] 10 Kohmreistor As shown Generic
  [3] Transistor In position shown Model
  [4] Diode TBC Model
  [5] Connector In position shown RS Model
  [6] PCB board As shown Model
