# Fritzing sketch refill_station_electronics_layout_v1 (saved by Fritzing 0.9.4)
perfboards: 1

parts:
  Mod1 = Raspberry Pi Pico
  J1 = Camdenboss CTB0158-3 [part_number=CTB0158-3 package=THT]
  J2 = Camdenboss CTB0158-6 [part_number=CTB0158-6 package=THT]
  Q1 = MOSFET-NCHANNEL [package=to220v]
  S1 = Square Pushbutton
  J3 = female pin header, 3 pins [form="♀ (female)"]
  VCC1 = Battery block 9V
  R2 = Resistor [tolerance=±1% resistance=100 package="1206 [SMD]"]
  M1 = DC Motor
  R3 = Resistor [tolerance=±5% resistance=10k package="1206 [SMD]"]
  D1 = Diode [package=diode-1n4001]  # not connected
  R1 = Rotary Potentiometer (Large) [maximum_resistance=100kΩ package=THT]
  C1 = Capacitor [package=axial-5mm]  # not connected
  C2 = Capacitor [package=axial-5mm]  # not connected
  C3 = Capacitor Polarized [package=panasonic_c]

nets:
  N1: Mod1.pin_3, Mod1.pin_8, Mod1.pin_13, Mod1.pin_18, Mod1.pin_23, Mod1.pin_28, Mod1.pin_33, Mod1.pin_38, J1.pin3, R3.Pin_1, C3.-
  N2: Mod1.pin_21, J2.pin6
  N3: Mod1.pin_29, R2.Pin_0
  N4: Mod1.pin_34, J1.pin2
  N5: Mod1.pin_35, J1.pin1
  N6: Mod1.pin_36, J2.pin5
  N7: Mod1.pin_39, J3.pin1, C3.+
  N8: J1.terminal_1, R1.leg1
  N9: J1.terminal_2, R1.wiper
  N10: J1.terminal_3, R1.leg2
  N11: J2.pin1, J3.pin3
  N12: J2.pin2, Q1.S, J3.pin2
  N13: J2.pin4, Q1.D
  N14: J2.terminal_1, VCC1.+
  N15: J2.terminal_2, VCC1.-
  N16: J2.terminal_3, M1.pin_1
  N17: J2.terminal_4, M1.pin_2
  N18: J2.terminal_5, S1.leg0
  N19: J2.terminal_6, S1.leg1
  N20: R2.Pin_1, R3.Pin_0

custom parts:
  Raspberry Pi Pico: Raspberry Pi Pico. Based around the RP2040 microcontroller the Pico is a low cost microcontroller device bringing Raspberry Pi quality, cost, and easy of use to the microcontroller space. Jan 2021, Split part in to two versions: tht (this one) and SMD. This one will drill holes for a .1 in header in pcb to allow plugging in the module as well as providing pads to solder the module to the top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
