# Fritzing sketch temp_refill_station_layout_test_v1 (saved by Fritzing 0.9.4)
perfboards: 1
breadboards: 1

parts:
  Q3 = MOSFET-NCHANNEL [package=to220v]
  Terminal_block1 = Camdenboss CTB0158-7 [part_number=CTB0158-7 package=THT]
  12V1 = Battery block 9V
  M2 = DC Motor
  R3 = Resistor [tolerance=±5% resistance=100 package=THT]
  R4 = Resistor [tolerance=±5% resistance=10k package=THT]  # not connected
  D3 = Schottky Diode [part_number=1N5817 package="300 mil [THT]"]
  R5 = Rotary Potentiometer (Small) [maximum_resistance=100kΩ package=THT]
  S2 = Pushbutton [package="[SMD]"]
  Mod2 = Raspberry Pi Pico
  C3 = Capacitor [package=axial-5mm]  # not connected
  C4 = Capacitor [package=axial-5mm]
  C5 = Capacitor [package=axial-5mm]  # not connected
  C6 = Capacitor [package=axial-5mm]  # not connected

nets:
  N1: Q3.G, R3.Pin_0
  N2: Q3.D, Terminal_block1.pin5
  N3: Q3.S, Terminal_block1.pin1
  N4: Terminal_block1.pin3, Terminal_block1.pin4
  N5: Terminal_block1.pin6, R3.Pin_1
  N6: Terminal_block1.terminal_1, R5.leg1, R5.wiper, R5.leg2, Mod2.pin_3, Mod2.pin_8, Mod2.pin_13, Mod2.pin_18, Mod2.pin_23, Mod2.pin_28, Mod2.pin_32, Mod2.pin_33, Mod2.pin_34, Mod2.pin_35, Mod2.pin_38, Mod2.pin_42
  N7: Terminal_block1.terminal_2, 12V1.-
  N8: Terminal_block1.terminal_3, 12V1.+
  N9: Terminal_block1.terminal_4, M2.pin_1
  N10: Terminal_block1.terminal_5, M2.pin_2
  N11: Terminal_block1.terminal_6, Mod2.pin_29
  N12: D3.cathode, C4.2
  N13: S2.Pin_1, S2.Pin_2, Mod2.pin_36
  N14: S2.Pin_3, S2.Pin_4, Mod2.pin_21

notes:
  Note pico is powered by usb or seperate power supply in this test setup!
  Note for unknown capacitor value across motor, then try soldering some female headers, and you can change the value as an experiment! But make sure the headers are the right width apart!

custom parts:
  Raspberry Pi Pico: Raspberry Pi Pico. Based around the RP2040 microcontroller the Pico is a low cost microcontroller device bringing Raspberry Pi quality, cost, and easy of use to the microcontroller space. Jan 2021, Split part in to two versions: tht (this one) and SMD. This one will drill holes for a .1 in header in pcb to allow plugging in the module as well as providing pads to solder the module to the top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
